// Logisim project partial-store.circ as structural Verilog: 2 circuits, main circuit partial_store
module partial_store (
  input  [31:0] Instruction,
  input  [31:0] MemAddress,
  input  [31:0] DataFromReg,
  input  MemRW,
  output [3:0] MemWriteMask,
  output [31:0] DataToMem
);

  wire [31:0] sb_data, sh_data;

  Multiplexer #(.select(2), .width(32)) multiplexer_1 (
    .in0({{24{1'b0}}, DataFromReg[7:0]}), .in1({{16{1'b0}}, DataFromReg[7:0], {8{1'b0}}}),
    .in2({{8{1'b0}}, DataFromReg[7:0], {16{1'b0}}}), .in3({DataFromReg[7:0], {24{1'b0}}}), .out(sb_data),
    .sel(MemAddress[1:0]));
  Multiplexer #(.select(2), .width(32)) multiplexer_2 (
    .in0({{16{1'b0}}, DataFromReg[15:0]}), .in1({{8{1'b0}}, DataFromReg[15:0], {8{1'b0}}}),
    .in2({DataFromReg[15:0], {16{1'b0}}}), .out(sh_data), .sel(MemAddress[1:0]));  // open: in3
  Multiplexer #(.select(2), .width(32)) multiplexer_3 (
    .in0(sb_data), .in1(sh_data), .in2(DataFromReg), .out(DataToMem), .sel(Instruction[13:12]));  // open: in3
  MemWriteMaskGen memwritemaskgen_1 (
    .store_sel(Instruction[13:12]), .Mem01(MemAddress[1:0]), .MemRW(MemRW), .MemWriteMask(MemWriteMask));

  // Other names for the same wires on the sheet: sb07[7:0] = DataFromReg[7:0]; sh015[15:0] = DataFromReg[15:0];
  //   sw_data[31:0] = DataFromReg; Opcode[6:0] = Instruction[6:0]; Funct3[2:0] = Instruction[14:12];
  //   store_sel[1:0] = Instruction[13:12]; Funct7[6:0] = Instruction[31:25]; Mem01[1:0] = MemAddress[1:0]

  // Notes on the sheet:
  //   INPUTS to your circuit
  //   DON'T CHANGE THE LOCATIONS OF THE INPUTS AND OUTPUTS!
  //   sb 00 sh 01 lw 10
  //   OUTPUT from your circuit
endmodule

module MemWriteMaskGen (
  input  [1:0] store_sel,
  input  [1:0] Mem01,
  input  MemRW,
  output [3:0] MemWriteMask
);

  wire and_1_out, and_2_out, and_3_out, and_4_out, and_5_out, and_6_out, and_7_out, and_8_out, and_9_out,
       and_10_out, and_11_out, not_1_out, not_2_out, not_3_out, not_4_out;

  not not_1 (not_1_out, store_sel[1]);
  not not_2 (not_2_out, store_sel[0]);
  not not_3 (not_3_out, Mem01[1]);
  not not_4 (not_4_out, Mem01[0]);
  and and_1 (and_1_out, store_sel[1], not_2_out, MemRW);
  and and_2 (and_2_out, not_2_out, Mem01[1], Mem01[0], MemRW);
  and and_3 (and_3_out, not_1_out, store_sel[0], Mem01[1], not_4_out, MemRW);
  and and_4 (and_4_out, store_sel[1], not_2_out, MemRW);
  and and_5 (and_5_out, not_1_out, store_sel[0], not_3_out, Mem01[0], MemRW);
  and and_6 (and_6_out, not_1_out, Mem01[1], not_4_out, MemRW);
  and and_7 (and_7_out, store_sel[1], not_2_out, MemRW);
  and and_8 (and_8_out, not_1_out, store_sel[0], not_3_out, MemRW);
  and and_9 (and_9_out, not_2_out, not_3_out, Mem01[0], MemRW);
  and and_10 (and_10_out, store_sel[1], not_2_out, MemRW);
  and and_11 (and_11_out, not_1_out, not_3_out, not_4_out, MemRW);
  or or_1 (MemWriteMask[3], and_1_out, and_2_out, and_3_out);
  or or_2 (MemWriteMask[2], and_4_out, and_5_out, and_6_out);
  or or_3 (MemWriteMask[1], and_7_out, and_8_out, and_9_out);
  or or_4 (MemWriteMask[0], and_10_out, and_11_out);
endmodule
