// Logisim project regfile.circ as structural Verilog: 1 circuit, main circuit regfile
module regfile (
  input  [4:0] ReadIndex1,
  input  [4:0] ReadIndex2,
  input  [4:0] WriteIndex,
  input  [31:0] WriteData,
  input  RegWEn,
  input  clk,
  output [31:0] ra,
  output [31:0] sp,
  output [31:0] t0,
  output [31:0] t1,
  output [31:0] t2,
  output [31:0] s0,
  output [31:0] s1,
  output [31:0] a0,
  output [31:0] ReadData1,
  output [31:0] ReadData2
);

  wire RegWEn0, RegWEn1, RegWEn2, RegWEn3, RegWEn4, RegWEn5, RegWEn6, RegWEn7, RegWEn8, RegWEn9, RegWEn10,
       RegWEn11, RegWEn12, RegWEn13, RegWEn14, RegWEn15, RegWEn16, RegWEn17, RegWEn18, RegWEn19, RegWEn20,
       RegWEn21, RegWEn22, RegWEn23, RegWEn24, RegWEn25, RegWEn26, RegWEn27, RegWEn28, RegWEn29, RegWEn30,
       RegWEn31;
  wire [31:0] x0, x3_gp, x4_tp, x11_a1, x12_a2, x13_a3, x14_a4, x15_a5, x16_a6, x17_a7, x18_s2, x19_s3,
       x20_s4, x21_s5, x22_s6, x23_s7, x24_s8, x25_s9, x26_s10, x27_s11, x28_t3, x29_t4, x30_t5, x31_t6;

  Register #(.width(32)) register_1 (.D(WriteData), .en(1'b0), .clk(clk), .Q(x0));  // open: clr
  Register #(.width(32)) register_2 (.D(WriteData), .en(RegWEn4), .clk(clk), .Q(x4_tp));  // open: clr
  Register #(.width(32)) register_3 (.D(WriteData), .en(RegWEn8), .clk(clk), .Q(s0));  // open: clr
  Register #(.width(32)) register_4 (.D(WriteData), .en(RegWEn12), .clk(clk), .Q(x12_a2));  // open: clr
  Register #(.width(32)) register_5 (.D(WriteData), .en(RegWEn16), .clk(clk), .Q(x16_a6));  // open: clr
  Register #(.width(32)) register_6 (.D(WriteData), .en(RegWEn20), .clk(clk), .Q(x20_s4));  // open: clr
  Register #(.width(32)) register_7 (.D(WriteData), .en(RegWEn24), .clk(clk), .Q(x24_s8));  // open: clr
  Register #(.width(32)) register_8 (.D(WriteData), .en(RegWEn28), .clk(clk), .Q(x28_t3));  // open: clr
  Register #(.width(32)) register_9 (.D(WriteData), .en(RegWEn1), .clk(clk), .Q(ra));  // open: clr
  Register #(.width(32)) register_10 (.D(WriteData), .en(RegWEn5), .clk(clk), .Q(t0));  // open: clr
  Register #(.width(32)) register_11 (.D(WriteData), .en(RegWEn9), .clk(clk), .Q(s1));  // open: clr
  Register #(.width(32)) register_12 (.D(WriteData), .en(RegWEn13), .clk(clk), .Q(x13_a3));  // open: clr
  Register #(.width(32)) register_13 (.D(WriteData), .en(RegWEn17), .clk(clk), .Q(x17_a7));  // open: clr
  Register #(.width(32)) register_14 (.D(WriteData), .en(RegWEn21), .clk(clk), .Q(x21_s5));  // open: clr
  Register #(.width(32)) register_15 (.D(WriteData), .en(RegWEn25), .clk(clk), .Q(x25_s9));  // open: clr
  Register #(.width(32)) register_16 (.D(WriteData), .en(RegWEn29), .clk(clk), .Q(x29_t4));  // open: clr
  Multiplexer #(.select(5), .width(32)) multiplexer_1 (
    .in0(x0), .in1(ra), .in2(sp), .in3(x3_gp), .in4(x4_tp), .in5(t0), .in6(t1), .in7(t2), .in8(s0), .in9(s1),
    .in10(a0), .in11(x11_a1), .in12(x12_a2), .in13(x13_a3), .in14(x14_a4), .in15(x15_a5), .in16(x16_a6),
    .in17(x17_a7), .in18(x18_s2), .in19(x19_s3), .in20(x20_s4), .in21(x21_s5), .in22(x22_s6), .in23(x23_s7),
    .in24(x24_s8), .in25(x25_s9), .in26(x26_s10), .in27(x27_s11), .in28(x28_t3), .in29(x29_t4),
    .in30(x30_t5), .in31(x31_t6), .out(ReadData1), .sel(ReadIndex1));
  Register #(.width(32)) register_17 (.D(WriteData), .en(RegWEn2), .clk(clk), .Q(sp));  // open: clr
  Register #(.width(32)) register_18 (.D(WriteData), .en(RegWEn6), .clk(clk), .Q(t1));  // open: clr
  Register #(.width(32)) register_19 (.D(WriteData), .en(RegWEn10), .clk(clk), .Q(a0));  // open: clr
  Register #(.width(32)) register_20 (.D(WriteData), .en(RegWEn14), .clk(clk), .Q(x14_a4));  // open: clr
  Register #(.width(32)) register_21 (.D(WriteData), .en(RegWEn18), .clk(clk), .Q(x18_s2));  // open: clr
  Register #(.width(32)) register_22 (.D(WriteData), .en(RegWEn22), .clk(clk), .Q(x22_s6));  // open: clr
  Register #(.width(32)) register_23 (.D(WriteData), .en(RegWEn26), .clk(clk), .Q(x26_s10));  // open: clr
  Register #(.width(32)) register_24 (.D(WriteData), .en(RegWEn30), .clk(clk), .Q(x30_t5));  // open: clr
  Register #(.width(32)) register_25 (.D(WriteData), .en(RegWEn3), .clk(clk), .Q(x3_gp));  // open: clr
  Register #(.width(32)) register_26 (.D(WriteData), .en(RegWEn7), .clk(clk), .Q(t2));  // open: clr
  Register #(.width(32)) register_27 (.D(WriteData), .en(RegWEn11), .clk(clk), .Q(x11_a1));  // open: clr
  Register #(.width(32)) register_28 (.D(WriteData), .en(RegWEn15), .clk(clk), .Q(x15_a5));  // open: clr
  Register #(.width(32)) register_29 (.D(WriteData), .en(RegWEn19), .clk(clk), .Q(x19_s3));  // open: clr
  Register #(.width(32)) register_30 (.D(WriteData), .en(RegWEn23), .clk(clk), .Q(x23_s7));  // open: clr
  Register #(.width(32)) register_31 (.D(WriteData), .en(RegWEn27), .clk(clk), .Q(x27_s11));  // open: clr
  Register #(.width(32)) register_32 (.D(WriteData), .en(RegWEn31), .clk(clk), .Q(x31_t6));  // open: clr
  Multiplexer #(.select(5), .width(32)) multiplexer_2 (
    .in0(x0), .in1(ra), .in2(sp), .in3(x3_gp), .in4(x4_tp), .in5(t0), .in6(t1), .in7(t2), .in8(s0), .in9(s1),
    .in10(a0), .in11(x11_a1), .in12(x12_a2), .in13(x13_a3), .in14(x14_a4), .in15(x15_a5), .in16(x16_a6),
    .in17(x17_a7), .in18(x18_s2), .in19(x19_s3), .in20(x20_s4), .in21(x21_s5), .in22(x22_s6), .in23(x23_s7),
    .in24(x24_s8), .in25(x25_s9), .in26(x26_s10), .in27(x27_s11), .in28(x28_t3), .in29(x29_t4),
    .in30(x30_t5), .in31(x31_t6), .out(ReadData2), .sel(ReadIndex2));
  Decoder #(.select(5)) decoder_1 (
    .out0(RegWEn0), .out1(RegWEn1), .out2(RegWEn2), .out3(RegWEn3), .out4(RegWEn4), .out5(RegWEn5),
    .out6(RegWEn6), .out7(RegWEn7), .out8(RegWEn8), .out9(RegWEn9), .out10(RegWEn10), .out11(RegWEn11),
    .out12(RegWEn12), .out13(RegWEn13), .out14(RegWEn14), .out15(RegWEn15), .out16(RegWEn16),
    .out17(RegWEn17), .out18(RegWEn18), .out19(RegWEn19), .out20(RegWEn20), .out21(RegWEn21),
    .out22(RegWEn22), .out23(RegWEn23), .out24(RegWEn24), .out25(RegWEn25), .out26(RegWEn26),
    .out27(RegWEn27), .out28(RegWEn28), .out29(RegWEn29), .out30(RegWEn30), .out31(RegWEn31),
    .sel(WriteIndex), .en(RegWEn));

  // Other names for the same wires on the sheet: x1_ra[31:0] = ra; x2_sp[31:0] = sp; x5_t0[31:0] = t0;
  //   x6_t1[31:0] = t1; x7_t2[31:0] = t2; x8_s0[31:0] = s0; x9_s1[31:0] = s1; x10_a0[31:0] = a0

  // Notes on the sheet:
  //   INPUTS to your circuit
  //   DON'T CHANGE THE LOCATIONS OF THE INPUTS AND OUTPUTS!
  //   These are DEBUG/TEST outputs from your circuit.
  //   OUTPUTS from your circuit
endmodule
